// Logisim project bikelight.circ as structural Verilog: 9 circuits, main circuit spec
module spec (
);

  wire Button_out;

  Button Button (.out(Button_out));
  main main_1 (.Button(Button_out));  // open: LED_2, LED
endmodule

module main (
  input  Button,
  output LED,
  output LED_2
);

  wire CLK_out, counter_4_1_out_0, counter_4_1_out_1, counter_multi_1_blink, counter_multi_1_pwm,
       debouncer_1_out, mux_1_out, synchronizer_1_out;

  Clock CLK (.out(CLK_out));
  counter_multi counter_multi_1 (.CLK(CLK_out), .Blink(counter_multi_1_blink), .PWM(counter_multi_1_pwm));
  synchronizer synchronizer_1 (.CLK(CLK_out), .In(debouncer_1_out), .Out(synchronizer_1_out));
  debouncer debouncer_1 (.In(Button), .Out(debouncer_1_out));
  counter_4 counter_4_1 (.In(synchronizer_1_out), .Out_0(counter_4_1_out_0), .Out_1(counter_4_1_out_1));
  mux mux_1 (
    .S0(counter_4_1_out_0), .S1(counter_4_1_out_1), .A(counter_multi_1_blink), .B(counter_multi_1_pwm),
    .Out(mux_1_out));
  driver driver_1 (.Enable(mux_1_out), .LED_Out(LED_2));

  assign LED = 1'b1;
endmodule

module counter_multi (
  input  CLK,
  output PWM,
  output Blink
);

  wire DFF0_nq, DFF0_q, DFF1_nq, DFF1_q, DFF2_nq, DFF2_q, DFF3_nq, DFF3_q, DFF4_nq, DFF4_q, DFF5_nq, DFF5_q,
       DFF6_nq, DFF6_q, DFF7_nq, DFF7_q, DFF8_nq, DFF8_q, DFF9_nq, DFF9_q, DFF10_nq, DFF10_q, DFF11_nq;

  dff DFF0 (.CLK(CLK), .D(DFF0_nq), .Q(DFF0_q), .nQ(DFF0_nq));
  dff DFF4 (.CLK(DFF3_q), .D(DFF4_nq), .Q(DFF4_q), .nQ(DFF4_nq));
  dff DFF8 (.CLK(DFF7_q), .D(DFF8_nq), .Q(DFF8_q), .nQ(DFF8_nq));
  dff DFF1 (.CLK(DFF0_q), .D(DFF1_nq), .Q(DFF1_q), .nQ(DFF1_nq));
  dff DFF5 (.CLK(DFF4_q), .D(DFF5_nq), .Q(DFF5_q), .nQ(DFF5_nq));
  dff DFF9 (.CLK(DFF8_q), .D(DFF9_nq), .Q(DFF9_q), .nQ(DFF9_nq));
  dff DFF2 (.CLK(DFF1_q), .D(DFF2_nq), .Q(DFF2_q), .nQ(DFF2_nq));
  dff DFF6 (.CLK(DFF5_q), .D(DFF6_nq), .Q(DFF6_q), .nQ(DFF6_nq));
  dff DFF10 (.CLK(DFF9_q), .D(DFF10_nq), .Q(DFF10_q), .nQ(DFF10_nq));
  dff DFF3 (.CLK(DFF2_q), .D(DFF3_nq), .Q(DFF3_q), .nQ(DFF3_nq));
  dff DFF7 (.CLK(DFF6_q), .D(DFF7_nq), .Q(DFF7_q), .nQ(DFF7_nq));
  dff DFF11 (.CLK(DFF10_q), .D(DFF11_nq), .Q(Blink), .nQ(DFF11_nq));
  nand nand_1 (PWM, DFF6_nq, DFF5_q);
endmodule

module debouncer (
  input  In,
  output Out
);


  assign Out = In;
endmodule

module counter_4 (
  input  In,
  output Out_0,
  output Out_1
);

  wire DFF0_q;

  dff DFF0 (.CLK(In), .D(Out_0), .Q(DFF0_q), .nQ(Out_0));
  dff DFF0_2 (.CLK(DFF0_q), .D(Out_1), .nQ(Out_1));  // open: Q
endmodule

module mux (
  input  S0,
  input  S1,
  input  A,
  input  B,
  output Out
);

  wire nand_1_out, nand_3_out, nand_4_out, not_1_out, not_2_out;

  not not_1 (not_1_out, S0);
  not not_2 (not_2_out, S1);
  nand nand_1 (nand_1_out, S0, not_2_out);
  nand nand_2 (Out, nand_1_out, nand_3_out, nand_4_out);
  nand nand_3 (nand_3_out, not_1_out, S1, A);
  nand nand_4 (nand_4_out, S0, S1, B);
endmodule

module driver (
  input  Enable,
  output LED_Out
);

  wire not_1_out, not_2_out;

  not not_1 (not_1_out, Enable);
  Transistor #(.\type ("n")) transistor_1 (.in(1'b0), .out(LED_Out), .gate(not_2_out));
  not not_2 (not_2_out, not_1_out);
endmodule

module synchronizer (
  input  CLK,
  input  In,
  output Out
);

  wire dff_1_q;

  dff dff_1 (.CLK(CLK), .D(In), .Q(dff_1_q));  // open: nQ
  dff dff_2 (.CLK(CLK), .D(dff_1_q), .Q(Out));  // open: nQ
endmodule

module dff (
  input  CLK,
  input  D,
  output Q,
  output nQ
);

  D_Flip_Flop d_ff_1 (.clk(CLK), .D(D), .Q(Q), .Qn(nQ));  // open: preset, en, reset
endmodule
